// Logisim project counter.circ as structural Verilog: 1 circuit, main circuit main
module main (
  input  clear,
  input  en,
  output carry,
  output [3:0] Q
);

  wire clk;
  wire [3:0] adder_1_out, multiplexer_1_out;

  Clock clock_1 (.out(clk));
  Adder #(.width(4)) adder_1 (.a(Q), .b(4'b0001), .out(adder_1_out), .cout(carry));  // open: cin
  Multiplexer #(.width(4)) multiplexer_1 (
    .in0(adder_1_out), .in1(4'b0000), .out(multiplexer_1_out), .sel(clear));  // open: en
  Register #(.width(4)) register_1 (.D(multiplexer_1_out), .en(en), .Q(Q), .clk(clk));  // open: clr

  // Other names for the same wires on the sheet: co = carry
endmodule
